# Fritzing sketch pressure (saved by Fritzing 1.0.1rc)
circuit board: 7.9cm x 4.8cm
breadboards: 1

parts:
  LLC1 = Logic Level Converter [package="Breakout board"]
  DC-DC = Mini-360 DC-DC Buck converter [package=THT]
  ADS1115 = Adafruit ADS1115 16Bit I2C ADC [part_number="Adafruit #1085"]
  D1_Mini = WeMos D1 Mini
  L1 = LED - 3mm [color="Green (570nm)" current=0.030A package="3 mm [THT]"]
  L2 = LED - 3mm [color="Red (633nm)" current=0.030A package="3 mm [THT]"]
  R3 = Resistor [tolerance=±5% power=0.25W resistance=100k package=THT]
  R4 = Resistor [tolerance=±5% power=0.25W resistance=100k package=THT]
  R5 = Resistor [tolerance=±5% power=0.25W resistance=100k package=THT]
  S_+_- = Camdenboss CTB0158-3 [part_number=CTB0158-3 package=THT]
  S_+_-_2 = Camdenboss CTB0158-3 [part_number=CTB0158-3 package=THT]
  S_+_-_3 = Camdenboss CTB0158-3 [part_number=CTB0158-3 package=THT]
  R2 = Resistor [tolerance=±5% power=0.25W resistance=220 package=THT]
  R1 = Resistor [tolerance=±5% power=0.25W resistance=220 package=THT]
  + = Camdenboss CTB0158-2 [part_number=CTB0158-2 package=THT]

nets:
  N1: LLC1.LV, D1_Mini.3V3
  N2: LLC1.L-GND, LLC1.H-GND, DC-DC.OUT-, ADS1115.GND, D1_Mini.G, L1.cathode, L2.cathode, R3.Pin_1, R4.Pin_1, R5.Pin_1, S_+_-.pin1, S_+_-_2.pin1, S_+_-_3.pin1
  N3: LLC1.LV3, D1_Mini.D1
  N4: LLC1.LV4, D1_Mini.D2
  N5: LLC1.HV4, ADS1115.SDA
  N6: LLC1.HV3, ADS1115.SCL
  VDD: LLC1.HV, DC-DC.OUT+, ADS1115.VDD, D1_Mini.5V, S_+_-.pin2, S_+_-_2.pin2, S_+_-_3.pin2
  N7: DC-DC.IN-, +.pin1
  N8: DC-DC.IN+, +.pin2
  N9: ADS1115.AIN2, R3.Pin_0, S_+_-_3.pin3
  N10: ADS1115.AIN1, R5.Pin_0, S_+_-_2.pin3
  N11: ADS1115.AIN0, R4.Pin_0, S_+_-.pin3
  N12: D1_Mini.D5, R2.Pin_0
  N13: D1_Mini.D6, R1.Pin_0
  N14: L1.anode, R1.Pin_1
  N15: L2.anode, R2.Pin_1

custom parts:
  Logic Level Converter: 5V to/from 3.3V logic level converter
  Mini-360 DC-DC Buck converter: Mini-360 DC-DC Buck converter. Tiny buck step down voltage converter, input voltage 4.75 to 23V output 1 to 17V adjustable. Available from ebay and the like.
  Adafruit ADS1115 16Bit I2C ADC: For microcontrollers without an analog-to-digital converter or when you want a higher-precision ADC, the ADS1115 provides 16-bit precision at 860 samples/second over I2C. The chip can be configured as 4 single-ended input channels, or two differential channels. As a nice bonus, it even includes a programmable gain amplifier, up to x16, to help boost up smaller single/differential signals to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
